# Fritzing sketch Battery schematic (saved by Fritzing 1.0.5)
breadboards: 1

parts:
  Arduino_Nano = Arduino Nano (Rev3.0) (ICSP)
  R1 = Resistor [tolerance=±5% power=0.25W resistance=47k package=THT]
  18650 = 18650 battery holder [package=battery-18650-kit]
  R2 = Resistor [tolerance=±5% power=0.25W resistance=10k package=THT]
  R3 = Resistor [tolerance=±5% power=0.25W resistance=47k package=THT]
  R4 = Resistor [tolerance=±5% power=0.25W resistance=10k package=THT]
  AAA_Battery = Battery Holders [package=battery-aaa]
  R5 = Resistor [tolerance=±5% power=0.25W resistance=22 package=THT]
  R6 = Resistor [tolerance=±5% power=0.25W resistance=22 package=THT]
  MOSFET = PNP-Transistor [package="TO92 [THT]"]
  R7 = Resistor [tolerance=±5% power=0.25W resistance=220 package=THT]
  R8 = Resistor [tolerance=±5% power=0.25W resistance=10k package=THT]
  S1 = Pushbutton [package="[THT]"]
  S2 = Pushbutton [package="[THT]"]
  OLED_I2C1 = OLED 128x64 I2C Monochrome Display

nets:
  GND: Arduino_Nano.GND, 18650.-, R2.Pin_1, R4.Pin_1, AAA_Battery.-, MOSFET.E, R8.Pin_1, S1.Pin_3, S1.Pin_4, S2.Pin_3, S2.Pin_4, OLED_I2C1.GND
  N1: Arduino_Nano.D5, S1.Pin_1, S1.Pin_2
  N2: Arduino_Nano.D6, S2.Pin_2
  N3: Arduino_Nano.D7, R7.Pin_1
  N4: Arduino_Nano.A5, OLED_I2C1.SCK
  N5: Arduino_Nano.A4, OLED_I2C1.SDA
  N6: Arduino_Nano.A3, R3.Pin_1, R4.Pin_0
  N7: Arduino_Nano.A2, R1.Pin_1, R2.Pin_0
  5V: Arduino_Nano.5V, OLED_I2C1.VDD
  N8: R1.Pin_0, 18650.+
  N9: R3.Pin_0, AAA_Battery.+, R5.Pin_1, R6.Pin_1
  N10: R5.Pin_0, R6.Pin_0, MOSFET.B
  N11: MOSFET.C, R7.Pin_0, R8.Pin_0

custom parts:
  18650 battery holder: 18650 Battery Holder identical to the dual battery version.
